// Logisim project dhbw_cpu.circ as structural Verilog
module RAM (
  input  [7:0] Data_In,
  input  [4:0] Command,
  input  Takt,
  output [7:0] Output
);

  wire decoder_1_out1, decoder_1_out2, decoder_1_out3, or_1_out;
  wire [7:0] High_q, Low_q, Middel_q;

  Decoder #(.select(2)) decoder_1 (
    .out1(decoder_1_out1), .out2(decoder_1_out2), .out3(decoder_1_out3), .sel(Command[1:0]), .en(Command[2]));  // open: out0
  Register Low (.D(Data_In), .en(decoder_1_out1), .Q(Low_q), .clk(Takt));  // open: clr
  Register Middel (.D(Data_In), .en(decoder_1_out2), .Q(Middel_q), .clk(Takt));  // open: clr
  Register High (.D(Data_In), .en(decoder_1_out3), .Q(High_q), .clk(Takt));  // open: clr
  or or_1 (or_1_out, Command[3], Command[4]);
  RAM_part #(.addrWidth(24), .bus("separate")) ram_1 (
    .addr({High_q, Middel_q, Low_q}), .din(Data_In), .data(Output), .str(Command[3]), .sel(or_1_out),
    .clk(Takt), .ld(Command[4]));  // open: clr
  Pull_Resistor pull_resistor_1 (.node(Output));
endmodule
